# Fritzing sketch collar (saved by Fritzing 0.9.2b)
circuit board: 14cm x 18cm
breadboards: 1

parts:
  U1 = XBee  # not connected
  Pad1 = Pad [width=4.81574069292929 height=1.45729978181818 connect=center]  # not connected
  Pad2 = Pad [width=4.81574069292929 height=1.45729978181818 connect=center]
  Pad3 = Pad [width=4.81574069292929 height=1.45729978181818 connect=center]
  Pad4 = Pad [width=4.81574069292929 height=1.45729978181818 connect=center]
  Pad5 = Pad [width=4.81574069292929 height=1.45729978181818 connect=center]
  Pad6 = Pad [width=4.81574069292929 height=1.45729978181818 connect=center]
  Pad7 = Pad [width=4.81574069292929 height=1.45729978181818 connect=center]
  Pad8 = Pad [width=4.81574069292929 height=1.45729978181818 connect=center]
  Pad9 = Pad [width=4.81574069292929 height=1.45729978181818 connect=center]
  Pad10 = Pad [width=4.81574069292929 height=1.45729978181818 connect=center]
  Pad11 = Pad [width=4.81574069292929 height=1.45729978181818 connect=center]
  Pad12 = Pad [width=4.81574069292929 height=1.45729978181818 connect=center]
  Pad13 = Pad [width=4.81574069292929 height=1.45729978181818 connect=center]
  Pad14 = Pad [width=4.81574069292929 height=1.45729978181818 connect=center]  # not connected
  Pad15 = Pad [width=4.81574069292929 height=1.45729978181818 connect=center]
  Pad16 = Pad [width=4.81574069292929 height=1.45729978181818 connect=center]  # not connected
  Pad17 = Pad [width=4.81574069292929 height=1.45729978181818 connect=center]  # not connected
  Pad18 = Pad [width=4.81574069292929 height=1.45729978181818 connect=center]
  Pad19 = Pad [width=4.81574069292929 height=1.45729978181818 connect=center]
  Pad20 = Pad [width=4.81574069292929 height=1.45729978181818 connect=center]
  Pad21 = Pad [width=3 height=1 connect=center]
  Pad22 = Pad [width=3 height=1 connect=center]
  Pad23 = Pad [width=3 height=1 connect=center]
  Pad24 = Pad [width=3 height=1 connect=center]
  Pad25 = Pad [width=3 height=1 connect=center]
  Pad26 = Pad [width=3 height=1 connect=center]
  Pad27 = Pad [width=3 height=1 connect=center]
  Pad28 = Pad [width=3 height=1 connect=center]
  Pad29 = Pad [width=3 height=1 connect=center]  # not connected
  Pad30 = Pad [width=3 height=1 connect=center]
  Pad31 = Pad [width=3 height=14.5 connect=north]
  Pad32 = Pad [width=4.81574069292929 height=1.45729978181818 connect=center]
  Pad33 = Pad [width=4.81574069292929 height=1.45729978181818 connect=center]
  Pad34 = Pad [width=4.81574069292929 height=1.45729978181818 connect=center]
  Pad35 = Pad [width=4.81574069292929 height=1.45729978181818 connect=center]
  Pad36 = Pad [width=4.81574069292929 height=1.45729978181818 connect=center]  # not connected
  Pad37 = Pad [width=4.81574069292929 height=1.45729978181818 connect=center]  # not connected
  Part1 = Arduino Pro Mini v13
  Pad38 = Pad [width=4.8531146495677 height=3.36296098047415 connect=center]
  Pad39 = Pad [width=4.8531146495677 height=3.36296098047415 connect=center]
  J1 = double row female pin header, 4 pins [form="♀ (female)"]
  J2 = double row female pin header, 8 pins [form="♀ (female)"]
  J3 = longpad pin header, 5 pins [form="long pad"]
  J4 = female pin header, 4 pins [form="♀ (female)"]
  J5 = female pin header, 5 pins [form="♀ (female)"]
  J6 = longpad pin header, 10 pins [form="long pad"]
  J8 = female pin header, 2 pins [form="♀ (female)"]  # not connected
  J9 = female pin header, 2 pins [form="♀ (female)"]  # not connected
  J10 = female pin header, 2 pins [form="♀ (female)"]  # not connected
  J7 = female pin header, 6 pins [form="♀ (female)"]  # not connected
  J11 = female pin header, 2 pins [form="♀ (female)"]  # not connected
  J12 = female pin header, 2 pins [form="♀ (female)"]  # not connected
  J13 = female pin header, 2 pins [form="♀ (female)"]  # not connected

nets:
  N1: Pad2.pad, J6.pin2
  N2: Pad3.pad, J6.pin4
  N3: Pad4.pad, J6.pin3
  N4: Pad5.pad, J6.pin5
  N5: Pad6.pad, J6.pin7
  N6: Pad7.pad, J6.pin6
  N7: Pad8.pad, J6.pin8
  N8: Pad9.pad, J6.pin9
  N9: Pad10.pad, J6.pin10
  N10: Pad11.pad, J2.pin5
  N11: Pad12.pad, Pad26.pad, Pad31.pad, Part1.GND, J2.pin1, J4.pin1
  N12: Pad13.pad, J5.pin1
  N13: Pad15.pad, J5.pin3
  N14: Pad18.pad, J5.pin2
  N15: Pad19.pad, J5.pin4
  N16: Pad20.pad, J5.pin5
  N17: Pad21.pad, J4.pin3
  N18: Pad22.pad, J4.pin4
  N19: Pad23.pad, Pad39.pad
  N20: Pad24.pad, J1.pin4
  N21: Pad25.pad, J1.pin3
  N22: Pad27.pad, J4.pin2
  N23: Pad28.pad, Part1.VCC, J2.pin2
  N24: Pad30.pad, Pad38.pad
  N25: Pad32.pad, J2.pin8
  N26: Pad33.pad, J2.pin7
  N27: Pad34.pad, J2.pin6
  N28: Pad35.pad, J6.pin1
  N29: Part1.D0/TX, J2.pin4
  N30: Part1.D1/RX, J2.pin3
  N31: Part1.D11_PWM/MOSI, J1.pin1
  N32: Part1.D10_PWM/SS, J1.pin2
  N33: Part1.D6_PWM, J3.pin5
  N34: Part1.D5_PWM, J3.pin4
  N35: Part1.D4, J3.pin3
  N36: Part1.D3_PWM, J3.pin2
  N37: Part1.D2, J3.pin1
